# Fritzing sketch Circuit (saved by Fritzing 0.9.2b)
breadboards: 1

parts:
  Bauteil1 = Arduino Yun
  Q1 = NPN-Transistor [package="TO92 [THT]"]
  Q2 = NPN-Transistor [package="TO92 [THT]"]
  Q3 = NPN-Transistor [package="TO92 [THT]"]
  U1 = Voltage Regulator - 5V [package="TO220 [THT]"]
  LED1 = RGB LED - (4 legs) [package="5 mm [THT]"]
  VCC1 = Battery
  R1 = Resistor [tolerance=±1% resistance=1k package="0402 [SMD]"]
  R2 = Resistor [tolerance=±1% resistance=1k package="0402 [SMD]"]
  R3 = Resistor [tolerance=±1% resistance=1k package="0402 [SMD]"]

nets:
  GND: Bauteil1.GND, Q1.E, Q2.E, Q3.E, U1.GND, VCC1.-
  N1: Bauteil1.D3_PWM, R3.Pin_1
  N2: Bauteil1.D5_PWM, R2.Pin_1
  N3: Bauteil1.D6_PWM, R1.Pin_1
  N4: Bauteil1.VIN, U1.output_voltage
  N5: Q1.B, R3.Pin_0
  N6: Q1.C, LED1.blue_cathode
  N7: Q2.B, R2.Pin_0
  N8: Q2.C, LED1.red_cathode
  N9: Q3.B, R1.Pin_0
  N10: Q3.C, LED1.green_cathode
  N11: U1.input_voltage, LED1.common_anode, VCC1.+
